# Fritzing sketch SmartRoomControllerCKCooper (saved by Fritzing 1.0.0rc)
breadboards: 4

parts:
  Breadboard4 = Breadboard Split Power
  Breadboard5 = Breadboard Split Power
  A1 = Particle - Photon2
  Part1 = 12 NeoPixel Ring [part_number=1643]
  Neopixel1 = Adafruit RBG Smart Neopixel [package="DIP (Dual Inline) [THT]"]
  Neopixel2 = Adafruit RBG Smart Neopixel [package="DIP (Dual Inline) [THT]"]
  Neopixel3 = Adafruit RBG Smart Neopixel [package="DIP (Dual Inline) [THT]"]
  Neopixel4 = Adafruit RBG Smart Neopixel [package="DIP (Dual Inline) [THT]"]
  U1 = ENCODER_RGB [package=encoder_led_2]
  S1 = Pushbutton [package="[THT]"]
  R1 = Resistor [tolerance=±5% resistance=220 package="2010 [SMD]"]
  Part2 = Barometric Pressure Sensor - BMP180 Breakout (GY-68)
  OLED_I2C1 = OLED 128x64 I2C Monochrome Display
  S2 = Pushbutton [package="[THT]"]
  R2 = Resistor [tolerance=±5% resistance=220 package="2010 [SMD]"]
  D1 = LTE-302 [package=lte-302]
  R4 = Resistor [tolerance=±5% resistance=220 package="2010 [SMD]"]
  S3 = Pushbutton [package="[THT]"]
  U2 = SWITCH_SPDT [package=kps-1290]
  R5 = Resistor [tolerance=±5% resistance=220 package="2010 [SMD]"]

nets (from the schematic view):
  N1: Breadboard4.pin3Y, Breadboard4.pin15Y
  N2: Breadboard4.pin4Z, Breadboard4.pin20Z, Breadboard4.pin29Z
  N3: Breadboard4.pin17Y, Breadboard4.pin21Y, Breadboard4.pin29Y
  N4: Breadboard5.pin3Y, Breadboard5.pin15Y
  N5: Breadboard5.pin3Z, Breadboard5.pin11Z
  N6: A1.Pin_2, A1.Pin_31, U1.+
  GND: A1.Pin_4, A1.Pin_6, A1.Pin_30, A1.Pin_32, Part1.GND, Neopixel1.G, Neopixel2.G, Neopixel3.G, Neopixel4.G, U1.C, R1.Pin_0, Part2.GND, OLED_I2C1.GND, R2.Pin_0, R4.Pin_1, U2.S, R5.Pin_0
  N7: A1.Pin_10, U1.R
  N8: A1.Pin_11, U1.G
  N9: A1.Pin_12, U1.SW
  N10: A1.Pin_14, U1.A
  N11: A1.Pin_15, U1.B
  N12: A1.Pin_17, Part2.SDA, OLED_I2C1.SDA
  N13: A1.Pin_18, Part2.SCL, OLED_I2C1.SCK
  N14: A1.Pin_19, Neopixel1.In
  VCC: A1.Pin_20, S1.Pin_3, S1.Pin_4, Part2.VCC, OLED_I2C1.VDD, D1.C, U2.O
  N15: A1.Pin_21, A1.Pin_22, S2.Pin_3, S2.Pin_4, S3.Pin_3, S3.Pin_4
  N16: A1.Pin_23, U2.P
  N17: A1.Pin_26, Part1.VDD, Neopixel1.+, Neopixel2.+, Neopixel3.+, Neopixel4.+
  N18: Part1.IN, Neopixel4.O
  N19: Neopixel1.O, Neopixel2.In
  N20: Neopixel2.O, Neopixel3.In
  N21: Neopixel3.O, Neopixel4.In
  N22: S1.Pin_1, S1.Pin_2, R1.Pin_1
  N23: S2.Pin_1, S2.Pin_2, R2.Pin_1
  N24: D1.A, R4.Pin_0
  N25: S3.Pin_1, S3.Pin_2, R5.Pin_1

custom parts:
  Breadboard Split Power: A custom 6 pin per group power supply strip where the top row (ground) is all bussed together and the bottom row (+V) is split in two groups of 12 pins. This version is modified to be a loadable part and was rescaled to be on the standard 1px = 1thou grid with the size set in inches
  Particle - Photon2: The Photon 2 is a microcontroller and Wi-Fi networking developed by particle. Features: 802.11a/b/g/n Wi-Fi, 2.4 GHz and 5 GHz Integrated PCB antenna Integrated U.FL connector for external antenna Integrated RF switch BLE 5 using same antenna as Wi-Fi Realtek RTL8721DM MCU ARM Cortex M33 CPU, 200 MHz 2048 KB (2 MB) user application maximum size 3072 KB (3 MB) of RAM available to user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
  12 NeoPixel Ring: 12 ultra bright smart LED NeoPixels are arranged in a circle with 1.5" (37mm) outer diameter. The rings are 'chainable' - connect the output pin of one to the input pin of another. Use only one microcontroller pin to control as many as you can chain together! Each LED is addressable as the driver chip is inside the LED. Each one has ~18mA constant current drive so the color will be very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
  ENCODER_RGB: SparkFun RGB rotary Encoder
  Pushbutton: A generic pushbutton.
